// Logisim project exercise.circ as structural Verilog: 3 circuits, main circuit main
module main (
  input  in_1,
  input  in_2,
  input  in_3,
  input  in_4,
  input  in_5,
  input  in_6,
  input  in_7,
  input  in_8,
  input  in_9,
  input  in_10,
  input  in_11,
  input  in_12,
  input  in_13,
  input  in_14,
  input  in_15,
  input  in_16,
  input  in_17,
  input  in_18,
  input  in_19,
  input  in_20,
  input  in_21,
  input  in_22,
  input  in_23,
  input  in_24,
  input  in_25,
  output out_26,
  output out_27,
  output out_28,
  output out_29,
  output out_30,
  output out_31,
  output out_32,
  output out_33,
  output out_34,
  output out_35,
  output out_36,
  output out_37,
  output out_38,
  output out_39
);

  wire and_2_out, full_adder_2_out_5, full_adder_3_out_5, full_adder_4_out_5, full_adder_5_out_5,
       full_adder_6_out_5, full_adder_7_out_5, half_adder_2_carry;

  or or_1 (out_26, in_1, in_2);
  and and_1 (out_27, in_3, in_4);
  and and_2 (and_2_out, in_5, in_6);
  full_adder full_adder_1 (.carry_in(full_adder_2_out_5), .a(in_11), .b(in_10), .out_4(out_32), .out_5(out_31));
  full_adder full_adder_2 (
    .carry_in(full_adder_3_out_5), .a(in_13), .b(in_12), .out_4(out_33), .out_5(full_adder_2_out_5));
  nand nand_1 (out_28, and_2_out, in_7);
  half_adder half_adder_1 (.a(in_8), .b(in_9), .sum(out_29), .carry(out_30));
  full_adder full_adder_3 (
    .carry_in(full_adder_4_out_5), .a(in_15), .b(in_14), .out_4(out_34), .out_5(full_adder_3_out_5));
  full_adder full_adder_4 (
    .carry_in(full_adder_5_out_5), .a(in_17), .b(in_16), .out_4(out_35), .out_5(full_adder_4_out_5));
  full_adder full_adder_5 (
    .carry_in(full_adder_6_out_5), .a(in_19), .b(in_18), .out_4(out_36), .out_5(full_adder_5_out_5));
  full_adder full_adder_6 (
    .carry_in(full_adder_7_out_5), .a(in_21), .b(in_20), .out_4(out_37), .out_5(full_adder_6_out_5));
  full_adder full_adder_7 (
    .carry_in(half_adder_2_carry), .a(in_23), .b(in_22), .out_4(out_38), .out_5(full_adder_7_out_5));
  half_adder half_adder_2 (.a(in_25), .b(in_24), .sum(out_39), .carry(half_adder_2_carry));
endmodule

module half_adder (
  input  a,
  input  b,
  output sum,
  output carry
);

  xor xor_1 (sum, a, b);
  and and_1 (carry, a, b);
endmodule

module full_adder (
  input  carry_in,
  input  a,
  input  b,
  output out_4,
  output out_5
);

  wire half_adder_1_carry, half_adder_1_sum, half_adder_2_carry;

  half_adder half_adder_1 (.a(a), .b(b), .sum(half_adder_1_sum), .carry(half_adder_1_carry));
  half_adder half_adder_2 (.a(carry_in), .b(half_adder_1_sum), .sum(out_4), .carry(half_adder_2_carry));
  or or_1 (out_5, half_adder_1_carry, half_adder_2_carry);
endmodule
